# Fritzing sketch iot-plant-watering-bot-bb (saved by Fritzing 0.9.3b)
breadboards: 1

parts:
  Part1 = Photon
  U1 = Voltage Regulator - 5V [package="TO220 [THT]"]
  Power_plug1 = Power plug
  M1 = DC Motor
  Q1 = npn-Powertransistor [package="TO220 [THT]"]
  R1 = Resistor [tolerance=±5% resistance=1k package=THT]

nets:
  GND: Part1.GND, U1.GND, Power_plug1.GND, Q1.emitter
  N1: Part1.VIN, U1.output_voltage
  N2: Part1.D0, R1.Pin_1
  N3: U1.input_voltage, Power_plug1.VCC, M1.pin_2
  N4: M1.pin_1, Q1.collector
  N5: Q1.base, R1.Pin_0

notes:
  TIP122
  LM7805
  12VDC
  ADAFRUIT PID 1150
